# Fritzing sketch LoLGamePad Fritzing (saved by Fritzing 0.9.2b)
circuit board: 8.46667cm x 5.64444cm
breadboards: 1

parts:
  Pro_Micro1 = Pro Micro
  S1 = Round Pushbutton
  S2 = Round Pushbutton
  S3 = Round Pushbutton
  S4 = Round Pushbutton
  S5 = Round Pushbutton
  S6 = Round Pushbutton
  S7 = Round Pushbutton
  S8 = Round Pushbutton
  S9 = Round Pushbutton
  S10 = Round Pushbutton  # not connected
  LED2 = RGB LED (com. cathode, rgb) [package="5 mm [THT]"]
  MIC1 = Microphone  # not connected
  Composant1 = Thumb Joystick
  R1 = Resistor [tolerance=±5% resistance=220 package=THT]

nets:
  N1: Pro_Micro1.D4, LED2.red_anode
  N2: Pro_Micro1.D10, S4.leg0
  N3: Pro_Micro1.D14/MISO, S1.leg0
  N4: Pro_Micro1.D20/A2, Composant1.HORZ
  N5: Pro_Micro1.D21/A3, Composant1.VERT
  VCC: Pro_Micro1.VCC, Composant1.VCC
  GND: Pro_Micro1.GND, S1.leg1, S2.leg1, S3.leg1, S4.leg1, S5.leg1, S6.leg1, S7.leg1, S8.leg1, S9.leg1, Composant1.GND, R1.Pin_0
  N6: LED2.common_cathode, R1.Pin_1

notes:
  4
  R
  F
  Z
  3
  2
  D
  1
  E
  A

custom parts:
  Pro Micro: The SparkFun Pro Micro is a complete USB-based microcontoller development system, in a very small footprint, capable of implementing many types of projects. All programming can be done via the USB port.
